# Fritzing sketch BlinkRGB (saved by Fritzing 0.9.1b)
breadboards: 1

parts:
  Part1 = Arduino Uno (Rev3) - ICSP
  R1 = Resistor [tolerance=±5% resistance=330 package="0603 [SMD]"]
  R2 = Resistor [tolerance=±5% resistance=330 package="0603 [SMD]"]
  LED3 = RGB LED - (4 legs) [package="5 mm [THT]"]
  R3 = Resistor [tolerance=±5% resistance=330 package="0603 [SMD]"]

nets:
  N1: Part1.ICSP_MOSI, Part1.D11_PWM/MOSI, R3.Pin_0
  N2: Part1.D9_PWM, R2.Pin_1
  N3: Part1.D10_PWM/SS, R1.Pin_1
  N4: Part1.5V, LED3.common_anode
  N5: R1.Pin_0, LED3.green_cathode
  N6: R2.Pin_0, LED3.blue_cathode
  N7: LED3.red_cathode, R3.Pin_1
