# Fritzing sketch CAP (saved by Fritzing 0.9.1b)
breadboards: 1
perfboards: 1

parts:
  Part1 = Arduino Uno (Rev3) - ICSP
  R4 = Resistor [tolerance=±5% resistance=1M package=THT]
  LED1 = LED - 3mm [color="Red (633nm)" package="3 mm [THT]"]
  R5 = Resistor [tolerance=±5% resistance=330 package=THT]

nets:
  N1: Part1.D9_PWM, R5.Pin_1
  N2: Part1.GND, LED1.cathode
  N3: Part1.D2, R4.Pin_1
  N4: Part1.D4, R4.Pin_0
  N5: LED1.anode, R5.Pin_0
