# Fritzing sketch DHT (saved by Fritzing 0.9.1b)
breadboards: 1

parts:
  Part1 = Arduino Uno (Rev3) - ICSP
  J1 = Basic Servo
  RHT1 = Humidity and Temperature Sensor RHT03
  R2 = Resistor [tolerance=±5% resistance=10k package="1206 [SMD]"]
  R2_2 = Resistor [tolerance=±5% package="2010 [SMD]"]

nets:
  N1: Part1.D2, RHT1.Data-signal, R2.Pin_1, R2_2.Pin_1
  N2: Part1.D3_PWM, J1.pulse
  VCC: Part1.5V, J1.vcc, RHT1.Vcc, R2.Pin_0, R2_2.Pin_0
  GND: Part1.GND, J1.gnd, RHT1.GND_2
