# Fritzing sketch leds (saved by Fritzing 0.7.12b)
breadboards: 1

parts:
  R1 = Resistor [tolerance=±5% resistance=330 package="0805 [SMD]"]
  Arduino1 = Arduino
  R4 = Resistor [tolerance=±5% resistance=330 package="0805 [SMD]"]
  LED1 = LED - 5mm [color="Red (633nm)" package="5 mm [THT]"]
  LED2 = LED - 5mm [color="Green (570nm)" package="5 mm [THT]"]

nets:
  N1: R1.Pin_0, Arduino1.GND, R4.Pin_0
  N2: R1.Pin_1, LED1.cathode
  N3: Arduino1.D10, LED2.anode
  N4: Arduino1.D9, LED1.anode
  N5: R4.Pin_1, LED2.cathode
