# Fritzing sketch lightAndLed_2 (saved by Fritzing 0.9.3b)
breadboards: 1

parts:
  Arduino1 = Arduino
  LED1 = smd LED [color="Red (633nm)" package="0805 [SMD]"]
  LED2 = smd LED [color="Green (570nm)" package="0805 [SMD]"]
  R6 = Basic Photo-Resistor (Photocell) [package=THT]
  R7 = 1k Ω Resistor [package=THT]

nets:
  N1: Arduino1.GND, LED1.cathode, LED2.cathode, R6.pin_0
  N2: Arduino1.D12, LED1.anode
  N3: Arduino1.D11, LED2.anode
  N4: Arduino1.+5V, R7.Pin_1
  N5: Arduino1.A0, R6.pin_1, R7.Pin_0
