# Fritzing sketch LuxPixel (saved by Fritzing 0.9.1b)
breadboards: 1
perfboards: 1

parts:
  Arduino1 = Arduino Uno (Rev3)
  R9 = Photocell (LDR) [package=THT]
  R10 = Resistor [tolerance=±5% resistance=10k package=THT]
  LED2 = Super Flux RGB LED (com. cathode)  # not connected
  LED3 = Super Flux RGB LED (com. cathode)  # not connected
  LED4 = Super Flux RGB LED (com. cathode)  # not connected

nets:
  N1: Arduino1.A0, R9.pin_0, R10.Pin_0
  N2: Arduino1.GND, R10.Pin_1

notes:
  NEOPIXEL
  GND
  DATA
  5V
