# Fritzing sketch blink (saved by Fritzing 0.7.12b)
breadboards: 1

parts:
  Arduino1 = Arduino
  LED1 = LED - 3mm [color="Red (633nm)" package="3 mm [THT]"]
  R1 = Resistor [tolerance=±5% resistance=330 package="0805 [SMD]"]

nets:
  N1: Arduino1.GND, R1.Pin_0
  N2: Arduino1.D12, LED1.anode
  N3: LED1.cathode, R1.Pin_1
