# Fritzing sketch tempAndLed (saved by Fritzing 0.7.12b)
breadboards: 1

parts:
  Arduino1 = Arduino
  R3 = Resistor [tolerance=±5% resistance=10k package="0805 [SMD]"]
  R4 = Resistor [tolerance=±5% resistance=330 package="0805 [SMD]"]
  LED2 = LED - 5mm [color="Green (570nm)" package="5 mm [THT]"]
  R5 = Temperature Sensor (Thermistor) [thermistor_type=NTC package=THT]

nets:
  N1: Arduino1.D11, LED2.anode
  N2: Arduino1.+5V, R3.Pin_0
  N3: Arduino1.GND, R4.Pin_0, R5.pin_1
  N4: Arduino1.A0, R3.Pin_1, R5.pin_0
  N5: R4.Pin_1, LED2.cathode
