# Fritzing sketch PotRGB (saved by Fritzing 0.7.12b)
breadboards: 1

parts:
  Arduino1 = Arduino
  R5 = Trimmer Potentiometer [maximum_resistance=10kΩ package=THT]
  LED1 = RGB LED - (4 legs) [package="5 mm [THT]"]
  R6 = 330 Ω Resistor [package=THT]
  R7 = 330 Ω Resistor [package=THT]
  R8 = 330 Ω Resistor [package=THT]

nets:
  N1: Arduino1.D11, R6.Pin_0
  N2: Arduino1.D10, R7.Pin_0
  N3: Arduino1.D9, R8.Pin_0
  N4: Arduino1.+5V, R5.leg1, LED1.green_cathode
  N5: Arduino1.GND, R5.leg2
  N6: Arduino1.A0, R5.wiper
  N7: LED1.red_cathode, R6.Pin_1
  N8: LED1.common_anode, R7.Pin_1
  N9: LED1.blue_cathode, R8.Pin_1
