# Fritzing sketch lighAndServo (saved by Fritzing 0.7.12b)
breadboards: 1

parts:
  Arduino1 = Arduino
  R2 = Basic Photo-Resistor (Photocell) [package=THT]
  R3 = Resistor [tolerance=±5% resistance=10k package="0805 [SMD]"]
  J2 = Basic Servo

nets:
  N1: Arduino1.D9, J2.pulse
  +5V: Arduino1.+5V, R3.Pin_0, J2.vcc
  GND: Arduino1.GND, R2.pin_1, J2.gnd
  N2: Arduino1.A0, R2.pin_0, R3.Pin_1
