# Fritzing sketch noise skin (saved by Fritzing 0.9.3b)
circuit board: 6.88566cm x 5.36311cm
breadboards: 1

parts:
  Q1 = npn-Powertransistor [package="TO220 [THT]"]
  R8 = Resistor [resistance=1k tolerance=±5% package=THT]
  Arduino2 = Arduino Uno (Rev3)
  SP1 = SPEAKER [package=pcb_mount_speaker]
  R9 = Resistor [resistance=330k tolerance=±5% package=THT]

nets:
  N1: Q1.base, R8.Pin_1
  N2: Q1.collector, SP1.-
  N3: Q1.emitter, Arduino2.GND
  N4: R8.Pin_0, Arduino2.D9_PWM
  N5: Arduino2.A0, R9.Pin_1
  N6: Arduino2.5V, SP1.+, R9.Pin_0

// code stored in the sketch: npnPowerTransistor.ino
const int transistorPin = 9;    // connected to the base of the transistor

 void setup() {
   // set  the transistor pin as output:
   pinMode(transistorPin, OUTPUT);
 }

 void loop() {
   digitalWrite(transistorPin, HIGH);
   delay(1000);
   digitalWrite(transistorPin, LOW);
   delay(1000);
 }
