# Fritzing sketch BlinkRGBPOTBUT (saved by Fritzing 0.9.1b)
breadboards: 1

parts:
  Part1 = Arduino Uno (Rev3) - ICSP
  R1 = Resistor [tolerance=±5% resistance=330 package="0603 [SMD]"]
  R2 = Resistor [tolerance=±5% resistance=330 package="0603 [SMD]"]
  LED3 = RGB LED - (4 legs) [package="5 mm [THT]"]
  R3 = Resistor [tolerance=±5% resistance=330 package="0603 [SMD]"]
  R4 = TRIMPOT [package=3362u-2]
  S1 = Pushbutton [package="[THT]"]

nets:
  N1: Part1.A0, R4.WIPER
  N2: Part1.ICSP_MISO, Part1.D12/MISO, S1.Pin_3, S1.Pin_4
  N3: Part1.ICSP_MOSI, Part1.D11_PWM/MOSI, R3.Pin_0
  N4: Part1.D9_PWM, R2.Pin_1
  N5: Part1.D10_PWM/SS, R1.Pin_1
  N6: Part1.5V, LED3.common_anode, R4.CCW, S1.Pin_1, S1.Pin_2
  N7: Part1.GND, R4.CW
  N8: R1.Pin_0, LED3.green_cathode
  N9: R2.Pin_0, LED3.blue_cathode
  N10: LED3.red_cathode, R3.Pin_1
