# Fritzing sketch Blink (saved by Fritzing 0.9.1b)
breadboards: 1

parts:
  Part1 = Arduino Uno (Rev3) - ICSP
  LED1 = LED - 3mm [color="Red (633nm)" package="3 mm [THT]"]
  R1 = Resistor [tolerance=±5% resistance=330 package="0603 [SMD]"]
  LED2 = LED - 3mm [color="Green (570nm)" package="3 mm [THT]"]
  R2 = Resistor [tolerance=±5% resistance=330 package="0603 [SMD]"]

nets:
  N1: Part1.ICSP_MOSI, Part1.D11_PWM/MOSI, LED1.anode
  N2: Part1.D10_PWM/SS, LED2.anode
  N3: Part1.GND, R1.Pin_0, R2.Pin_0
  N4: LED1.cathode, R1.Pin_1
  N5: LED2.cathode, R2.Pin_1
