# Fritzing sketch LDR (saved by Fritzing 0.9.1b)
breadboards: 1

parts:
  Part1 = Arduino Uno (Rev3) - ICSP
  R1 = Photocell (LDR) [package=THT]
  R2 = Resistor [package="2010 [SMD]"]
  R2_2 = Resistor [tolerance=±5% resistance=220 package="1206 [SMD]"]
  R2_3 = Resistor [tolerance=±5% resistance=10k package="0805 [SMD]"]

nets:
  N1: Part1.A0, R1.pin_1, R2.Pin_0, R2_2.Pin_0, R2_3.Pin_0
  N2: Part1.5V, R1.pin_0
  N3: Part1.GND, R2.Pin_1, R2_2.Pin_1, R2_3.Pin_1
